// Digital circuit an_crtl.dig as structural Verilog
module an_crtl (
  input  CLK,
  output AN_3,
  output AN_2,
  output AN_1,
  output AN_0
);

  wire d_ff_1_nq, d_ff_1_q, d_ff_2_nq, not_1_out, not_2_out, not_3_out, not_4_out;

  D_FF d_ff_1 (.D(d_ff_1_nq), .C(CLK), .Q(d_ff_1_q), .nQ(d_ff_1_nq));
  D_FF d_ff_2 (.D(d_ff_2_nq), .C(d_ff_1_q), .nQ(d_ff_2_nq));  // open: Q
  not not_1 (not_1_out, d_ff_1_nq);
  and and_1 (AN_0, not_1_out, not_2_out);
  not not_2 (not_2_out, d_ff_2_nq);
  and and_2 (AN_1, d_ff_1_nq, not_3_out);
  not not_3 (not_3_out, d_ff_2_nq);
  and and_3 (AN_2, not_4_out, d_ff_2_nq);
  not not_4 (not_4_out, d_ff_1_nq);
  and and_4 (AN_3, d_ff_1_nq, d_ff_2_nq);

  // Notes on the sheet:
  //   CLK: default 1
endmodule
