// Digital circuit async_4bit_counter.dig as structural Verilog
module async_4bit_counter (
  input  IN,
  output S0,
  output S1,
  output S2,
  output S3
);

  wire d_ff_1_q, d_ff_2_q, d_ff_3_q, d_ff_4_nq;

  D_FF d_ff_1 (.D(S0), .C(IN), .Q(d_ff_1_q), .nQ(S0));
  D_FF d_ff_2 (.D(S1), .C(d_ff_1_q), .Q(d_ff_2_q), .nQ(S1));
  D_FF d_ff_3 (.D(S2), .C(d_ff_2_q), .Q(d_ff_3_q), .nQ(S2));
  D_FF d_ff_4 (.D(d_ff_4_nq), .C(d_ff_3_q), .Q(S3), .nQ(d_ff_4_nq));
endmodule
