// Digital circuit basys_clock.dig as structural Verilog
module basys_clock (
  input  Clock,
  input  Center,
  input  SW0,
  input  SW1,
  input  SW2,
  input  SW3,
  input  SW4,
  input  SW5,
  input  SW6,
  input  SW8,
  input  SW9,
  input  SW10,
  input  SW12,
  input  SW13,
  output AN3,
  output AN2,
  output AN1,
  output AN0,
  output CD,
  output CC,
  output CB,
  output CA,
  output CE,
  output CF,
  output CG,
  output DP,
  output JB1,
  output JB2,
  output JB3,
  output JB4,
  output JB7,
  output JB8,
  output JB9,
  output JB10
);

  wire hold_signal_1_out, or_1_out, register_1_q, register_2_q, register_3_q, register_4_q, register_5_q,
       register_6_q, seven_seg_cmpl_1_an_0, seven_seg_cmpl_1_an_1, seven_seg_cmpl_1_an_2,
       seven_seg_cmpl_1_an_3;
  wire [3:0] and_3_out, and_6_out, and_7_out, and_8_out, d_ff_2_q, d_ff_3_q, d_ff_4_q, d_ff_5_q,
       incr_4bit_1_out, incr_4bit_2_out, incr_4bit_3_out, incr_4bit_4_out, multiplexer_1_out,
       multiplexer_2_out, multiplexer_3_out, multiplexer_4_out;
  wire [3:3] comp_4bit_1_out, comp_4bit_2_out, comp_4bit_3_out, comp_4bit_4_out;
  wire [5:0] and_1_out, d_ff_1_q, incr_6bit_1_out;
  wire [5:5] comp_6bit_1_out;

  incr_6bit incr_6bit_1 (.IN(and_1_out), .EN(1'b1), .OUT(incr_6bit_1_out));
  assign and_1_out = d_ff_1_q & ~{6{comp_6bit_1_out[5]}};  // And and_1, 6 bits wide
  Register register_1 (.D(register_2_q), .C(Clock), .en(1'b1), .Q(register_1_q));
  Register register_2 (.D(comp_6bit_1_out[5]), .C(Clock), .en(1'b1), .Q(register_2_q));
  comp_6bit comp_6bit_1 (.B(d_ff_1_q), .A(6'b111100), .OUT(comp_6bit_1_out[5]));
  D_FF #(.Bits(6)) d_ff_1 (.D(incr_6bit_1_out), .C(Clock), .Q(d_ff_1_q));  // open: nQ
  hold_signal hold_signal_1 (.CLK(Clock), .In(register_3_q), .Wait(4'b0100), .Out(hold_signal_1_out));
  Register register_3 (.D(register_1_q), .C(Clock), .en(1'b1), .Q(register_3_q));
  and and_2 (JB9, hold_signal_1_out, ~JB1, ~JB7);  // And
  incr_4bit incr_4bit_1 (.IN(and_3_out), .EN(comp_6bit_1_out[5]), .OUT(incr_4bit_1_out));
  comp_4bit comp_4bit_1 (.B(multiplexer_1_out), .A(4'b1010), .OUT(comp_4bit_1_out[3]));
  assign and_3_out = multiplexer_1_out & ~{4{comp_4bit_1_out[3]}};  // And and_3, 4 bits wide
  and and_4 (JB4, JB1, ~JB7);  // And
  Register register_4 (.D(register_5_q), .C(Clock), .en(1'b1), .Q(register_4_q));
  Register register_5 (.D(comp_4bit_1_out[3]), .C(Clock), .en(1'b1), .Q(register_5_q));
  D_FF #(.Bits(4)) d_ff_2 (.D(incr_4bit_1_out), .C(Clock), .Q(d_ff_2_q));  // open: nQ
  hold_signal hold_signal_2 (.CLK(Clock), .In(register_4_q), .Wait(4'b0100), .Out(JB1));
  and and_5 (JB10, JB7, ~JB2);  // And
  incr_4bit incr_4bit_2 (.IN(and_6_out), .EN(comp_4bit_1_out[3]), .OUT(incr_4bit_2_out));
  Multiplexer #(.Bits(4)) multiplexer_1 (
    .sel(Center), .in_0(d_ff_2_q), .in_1({SW3, SW2, SW1, SW0}), .out(multiplexer_1_out));
  comp_4bit comp_4bit_2 (.B(multiplexer_2_out), .A(4'b0110), .OUT(comp_4bit_2_out[3]));
  assign and_6_out = multiplexer_2_out & ~{4{comp_4bit_2_out[3]}};  // And and_6, 4 bits wide
  hold_signal hold_signal_3 (.CLK(Clock), .In(register_6_q), .Wait(4'b1000), .Out(JB7));
  Register register_6 (.D(comp_4bit_2_out[3]), .C(Clock), .en(1'b1), .Q(register_6_q));
  D_FF #(.Bits(4)) d_ff_3 (.D(incr_4bit_2_out), .C(Clock), .Q(d_ff_3_q));  // open: nQ
  incr_4bit incr_4bit_3 (.IN(and_7_out), .EN(comp_4bit_2_out[3]), .OUT(incr_4bit_3_out));
  Multiplexer #(.Bits(4)) multiplexer_2 (
    .sel(Center), .in_0(d_ff_3_q), .in_1({1'b0, SW6, SW5, SW4}), .out(multiplexer_2_out));
  comp_4bit comp_4bit_3 (.B(multiplexer_3_out), .A(4'b0110), .OUT(comp_4bit_3_out[3]));
  assign and_7_out = multiplexer_3_out & ~{4{comp_4bit_3_out[3]}};  // And and_7, 4 bits wide
  D_FF #(.Bits(4)) d_ff_4 (.D(incr_4bit_3_out), .C(Clock), .Q(d_ff_4_q));  // open: nQ
  or or_1 (or_1_out, comp_4bit_3_out[3], register_6_q, register_4_q, register_3_q);
  hold_signal hold_signal_4 (.CLK(Clock), .In(comp_4bit_3_out[3]), .Wait(4'b1000), .Out(JB2));
  Multiplexer #(.Bits(4)) multiplexer_3 (
    .sel(Center), .in_0(d_ff_4_q), .in_1({1'b0, SW10, SW9, SW8}), .out(multiplexer_3_out));
  incr_4bit incr_4bit_4 (.IN(and_8_out), .EN(comp_4bit_3_out[3]), .OUT(incr_4bit_4_out));
  comp_4bit comp_4bit_4 (.B(multiplexer_4_out), .A(4'b0100), .OUT(comp_4bit_4_out[3]));
  assign and_8_out = multiplexer_4_out & ~{4{comp_4bit_4_out[3]}};  // And and_8, 4 bits wide
  hold_signal hold_signal_5 (.CLK(Clock), .In(or_1_out), .Wait(4'b0001), .Out(JB3));
  hold_signal hold_signal_6 (.CLK(Clock), .In(comp_4bit_4_out[3]), .Wait(4'b1000), .Out(JB8));
  D_FF #(.Bits(4)) d_ff_5 (.D(incr_4bit_4_out), .C(Clock), .Q(d_ff_5_q));  // open: nQ
  Multiplexer #(.Bits(4)) multiplexer_4 (
    .sel(Center), .in_0(d_ff_5_q), .in_1({2'b00, SW13, SW12}), .out(multiplexer_4_out));
  seven_seg_cmpl seven_seg_cmpl_1 (
    .SEG_3(multiplexer_4_out), .SEG_2(multiplexer_3_out), .SEG_1(multiplexer_2_out),
    .SEG_0(multiplexer_1_out), .CLK(Clock), .a(CA), .b(CB), .c(CC), .d(CD), .e(CE), .f(CF), .g(CG),
    .AN_3(seven_seg_cmpl_1_an_3), .AN_2(seven_seg_cmpl_1_an_2), .AN_1(seven_seg_cmpl_1_an_1),
    .AN_0(seven_seg_cmpl_1_an_0));
  not not_1 (AN0, seven_seg_cmpl_1_an_0);
  not not_2 (AN1, seven_seg_cmpl_1_an_1);
  not not_3 (AN2, seven_seg_cmpl_1_an_2);
  not not_4 (AN3, seven_seg_cmpl_1_an_3);

  assign DP = 1'b0;

  // Notes on the sheet:
  //   AN3: pin W4
  //   AN2: pin V4
  //   AN1: pin U4
  //   AN0: pin U2
  //   CD: pin V8
  //   CC: pin U8
  //   CB: pin W6
  //   CA: pin W7
  //   CE: pin U5
  //   CF: pin V5
  //   CG: pin U7
  //   DP: pin V7
  //   Clock: pin W5
  //   Center: pin U18
  //   SW0: pin V17
  //   SW1: pin V16
  //   SW2: pin W16
  //   SW3: pin W17
  //   SW4: pin W15
  //   SW5: pin V15
  //   SW6: pin W14
  //   SW8: pin V2
  //   SW9: pin T3
  //   SW10: pin T2
  //   SW12: pin W2
  //   SW13: pin U1
  //   JB1: pin A14
  //   JB2: pin A16
  //   JB3: pin B15
  //   JB4: pin B16
  //   JB7: pin A15
  //   JB8: pin A17
  //   JB9: pin C15
  //   JB10: pin C16
endmodule
