// Digital circuit broken_7seg.dig as structural Verilog
module broken_7seg (
);

  wire ANODE_out, PT_out, SW_0_out, SW_1_out, sw_2_6seg_1_p5, sw_2_6seg_1_p6, sw_2_6seg_1_p7, sw_2_6seg_1_p8,
       sw_2_6seg_1_p9, sw_2_6seg_1_p10, sw_2_6seg_1_p11, SW_2_out, SW_3_out;

  DipSwitch SW_0 (.out(SW_0_out));
  DipSwitch SW_1 (.out(SW_1_out));
  DipSwitch SW_2 (.out(SW_2_out));
  DipSwitch SW_3 (.out(SW_3_out));
  // sw_2_6seg sw_2_6seg_1: pin names not known; wires that end beside it: SW_0_out, SW_1_out, SW_2_out, SW_3_out, sw_2_6seg_1_p5, sw_2_6seg_1_p6, sw_2_6seg_1_p7, sw_2_6seg_1_p8, sw_2_6seg_1_p9, sw_2_6seg_1_p10, sw_2_6seg_1_p11
  Seven_Seg #(.commonConnectionType("anode"), .commonCathode("true")) seven_seg_1 (
    .a(sw_2_6seg_1_p5), .b(sw_2_6seg_1_p6), .c(sw_2_6seg_1_p7), .d(sw_2_6seg_1_p8), .e(sw_2_6seg_1_p9),
    .f(sw_2_6seg_1_p10), .g(sw_2_6seg_1_p11), .dp(PT_out), .common(ANODE_out));
  DipSwitch ANODE (.out(ANODE_out));
  DipSwitch PT (.out(PT_out));
endmodule
