// Digital circuit clock.dig as structural Verilog
module clock (
  input  clk,
  input  clk_2,
  input  in_3
);

  wire and_1_out, button_1_out, delay_1_out, delay_2_out, delay_3_out, delay_4_out, delay_5_out,
       multiplexer_1_out, multiplexer_2_out, multiplexer_4_out, multiplexer_7_out, seven_seg_cmpl_1_a,
       seven_seg_cmpl_1_an_0, seven_seg_cmpl_1_an_1, seven_seg_cmpl_1_an_2, seven_seg_cmpl_1_an_3,
       seven_seg_cmpl_1_b, seven_seg_cmpl_1_c, seven_seg_cmpl_1_d, seven_seg_cmpl_1_e, seven_seg_cmpl_1_f,
       seven_seg_cmpl_1_g;
  wire [1:0] dipswitch_11_out;
  wire [2:0] dipswitch_5_out, dipswitch_8_out;
  wire [3:0] d_ff_2_q, d_ff_3_q, d_ff_4_q, d_ff_5_q, dipswitch_1_out, incr_4bit_1_out, incr_4bit_2_out,
       incr_4bit_3_out, incr_4bit_4_out, multiplexer_3_out, multiplexer_5_out, multiplexer_6_out,
       multiplexer_8_out, or_2_out, or_3_out, or_4_out, or_5_out;
  wire [3:3] comp_4bit_1_out, comp_4bit_2_out, comp_4bit_3_out, comp_4bit_4_out;
  wire [5:0] d_ff_1_q, incr_6bit_1_out, or_1_out;
  wire [5:5] comp_6bit_1_out;

  and and_1 (and_1_out, clk, in_3);
  incr_6bit incr_6bit_1 (.IN(or_1_out), .EN(and_1_out), .OUT(incr_6bit_1_out));
  Delay #(.delayTime(20)) delay_1 (.in(and_1_out), .out(delay_1_out));
  comp_6bit comp_6bit_1 (.B(d_ff_1_q), .A(6'b111011), .OUT(comp_6bit_1_out[5]));
  assign or_1_out = d_ff_1_q | {6{comp_6bit_1_out[5]}};  // Or or_1, 6 bits wide
  D_FF #(.Bits(6)) d_ff_1 (.D(incr_6bit_1_out), .C(delay_1_out), .Q(d_ff_1_q));  // open: nQ
  incr_4bit incr_4bit_1 (.IN(or_2_out), .EN(comp_6bit_1_out[5]), .OUT(incr_4bit_1_out));
  Multiplexer multiplexer_1 (
    .sel(button_1_out), .in_0(comp_6bit_1_out[5]), .in_1(button_1_out), .out(multiplexer_1_out));
  comp_4bit comp_4bit_1 (.B(multiplexer_3_out), .A(4'b1001), .OUT(comp_4bit_1_out[3]));
  Delay #(.delayTime(20)) delay_2 (.in(multiplexer_1_out), .out(delay_2_out));
  assign or_2_out = multiplexer_3_out | {4{comp_4bit_1_out[3]}};  // Or or_2, 4 bits wide
  D_FF #(.Bits(4)) d_ff_2 (.D(incr_4bit_1_out), .C(delay_2_out), .Q(d_ff_2_q));  // open: nQ
  incr_4bit incr_4bit_2 (.IN(or_3_out), .EN(comp_4bit_1_out[3]), .OUT(incr_4bit_2_out));
  Multiplexer multiplexer_2 (
    .sel(button_1_out), .in_0(comp_4bit_1_out[3]), .in_1(button_1_out), .out(multiplexer_2_out));
  Multiplexer #(.Bits(4)) multiplexer_3 (
    .sel(button_1_out), .in_0(d_ff_2_q), .in_1(dipswitch_1_out), .out(multiplexer_3_out));
  Button button_1 (.out(button_1_out));
  comp_4bit comp_4bit_2 (.B(multiplexer_5_out), .A(4'b0101), .OUT(comp_4bit_2_out[3]));
  assign or_3_out = multiplexer_5_out | {4{comp_4bit_2_out[3]}};  // Or or_3, 4 bits wide
  Delay #(.delayTime(20)) delay_3 (.in(multiplexer_2_out), .out(delay_3_out));
  DipSwitch dipswitch_1 (.out(dipswitch_1_out[0]));
  DipSwitch dipswitch_2 (.out(dipswitch_1_out[1]));
  DipSwitch dipswitch_3 (.out(dipswitch_1_out[2]));
  D_FF #(.Bits(4)) d_ff_3 (.D(incr_4bit_2_out), .C(delay_3_out), .Q(d_ff_3_q));  // open: nQ
  DipSwitch dipswitch_4 (.out(dipswitch_1_out[3]));
  incr_4bit incr_4bit_3 (.IN(or_4_out), .EN(comp_4bit_2_out[3]), .OUT(incr_4bit_3_out));
  Multiplexer multiplexer_4 (
    .sel(button_1_out), .in_0(comp_4bit_2_out[3]), .in_1(button_1_out), .out(multiplexer_4_out));
  Multiplexer #(.Bits(4)) multiplexer_5 (
    .sel(button_1_out), .in_0(d_ff_3_q), .in_1({1'b0, dipswitch_5_out}), .out(multiplexer_5_out));
  DipSwitch dipswitch_5 (.out(dipswitch_5_out[0]));
  DipSwitch dipswitch_6 (.out(dipswitch_5_out[1]));
  DipSwitch dipswitch_7 (.out(dipswitch_5_out[2]));
  comp_4bit comp_4bit_3 (.B(multiplexer_6_out), .A(4'b0101), .OUT(comp_4bit_3_out[3]));
  Delay #(.delayTime(20)) delay_4 (.in(multiplexer_4_out), .out(delay_4_out));
  DipSwitch dipswitch_8 (.out(dipswitch_8_out[0]));
  assign or_4_out = multiplexer_6_out | {4{comp_4bit_3_out[3]}};  // Or or_4, 4 bits wide
  D_FF #(.Bits(4)) d_ff_4 (.D(incr_4bit_3_out), .C(delay_4_out), .Q(d_ff_4_q));  // open: nQ
  DipSwitch dipswitch_9 (.out(dipswitch_8_out[1]));
  DipSwitch dipswitch_10 (.out(dipswitch_8_out[2]));
  Multiplexer #(.Bits(4)) multiplexer_6 (
    .sel(button_1_out), .in_0(d_ff_4_q), .in_1({1'b0, dipswitch_8_out}), .out(multiplexer_6_out));
  DipSwitch dipswitch_11 (.out(dipswitch_11_out[0]));
  DipSwitch dipswitch_12 (.out(dipswitch_11_out[1]));
  incr_4bit incr_4bit_4 (.IN(or_5_out), .EN(comp_4bit_3_out[3]), .OUT(incr_4bit_4_out));
  Multiplexer multiplexer_7 (
    .sel(button_1_out), .in_0(comp_4bit_3_out[3]), .in_1(button_1_out), .out(multiplexer_7_out));
  comp_4bit comp_4bit_4 (.B(multiplexer_8_out), .A(4'b0011), .OUT(comp_4bit_4_out[3]));
  assign or_5_out = multiplexer_8_out | {4{comp_4bit_4_out[3]}};  // Or or_5, 4 bits wide
  Delay #(.delayTime(20)) delay_5 (.in(multiplexer_7_out), .out(delay_5_out));
  D_FF #(.Bits(4)) d_ff_5 (.D(incr_4bit_4_out), .C(delay_5_out), .Q(d_ff_5_q));  // open: nQ
  Multiplexer #(.Bits(4)) multiplexer_8 (
    .sel(button_1_out), .in_0(d_ff_5_q), .in_1({2'b00, dipswitch_11_out}), .out(multiplexer_8_out));
  seven_seg_cmpl seven_seg_cmpl_1 (
    .SEG_3(multiplexer_8_out), .SEG_2(multiplexer_6_out), .SEG_1(multiplexer_5_out),
    .SEG_0(multiplexer_3_out), .CLK(clk_2), .a(seven_seg_cmpl_1_a), .b(seven_seg_cmpl_1_b),
    .c(seven_seg_cmpl_1_c), .d(seven_seg_cmpl_1_d), .e(seven_seg_cmpl_1_e), .f(seven_seg_cmpl_1_f),
    .g(seven_seg_cmpl_1_g), .AN_3(seven_seg_cmpl_1_an_3), .AN_2(seven_seg_cmpl_1_an_2),
    .AN_1(seven_seg_cmpl_1_an_1), .AN_0(seven_seg_cmpl_1_an_0));
  Seven_Seg #(.commonConnectionType("anode"), .commonCathode("true")) seven_seg_1 (
    .a(seven_seg_cmpl_1_a), .b(seven_seg_cmpl_1_b), .c(seven_seg_cmpl_1_c), .d(seven_seg_cmpl_1_d),
    .e(seven_seg_cmpl_1_e), .f(seven_seg_cmpl_1_f), .g(seven_seg_cmpl_1_g), .dp(1'b0),
    .common(seven_seg_cmpl_1_an_3));
  Seven_Seg #(.commonConnectionType("anode"), .commonCathode("true")) seven_seg_2 (
    .a(seven_seg_cmpl_1_a), .b(seven_seg_cmpl_1_b), .c(seven_seg_cmpl_1_c), .d(seven_seg_cmpl_1_d),
    .e(seven_seg_cmpl_1_e), .f(seven_seg_cmpl_1_f), .g(seven_seg_cmpl_1_g), .dp(1'b0),
    .common(seven_seg_cmpl_1_an_2));
  Seven_Seg #(.commonConnectionType("anode"), .commonCathode("true")) seven_seg_3 (
    .a(seven_seg_cmpl_1_a), .b(seven_seg_cmpl_1_b), .c(seven_seg_cmpl_1_c), .d(seven_seg_cmpl_1_d),
    .e(seven_seg_cmpl_1_e), .f(seven_seg_cmpl_1_f), .g(seven_seg_cmpl_1_g), .dp(1'b0),
    .common(seven_seg_cmpl_1_an_1));
  Seven_Seg #(.commonConnectionType("anode"), .commonCathode("true")) seven_seg_4 (
    .a(seven_seg_cmpl_1_a), .b(seven_seg_cmpl_1_b), .c(seven_seg_cmpl_1_c), .d(seven_seg_cmpl_1_d),
    .e(seven_seg_cmpl_1_e), .f(seven_seg_cmpl_1_f), .g(seven_seg_cmpl_1_g), .dp(1'b0),
    .common(seven_seg_cmpl_1_an_0));

  // Notes on the sheet:
  //   clk: Hz: 10
  //   clk_2: Hz: 10
endmodule
