// Digital circuit comp_4bit.dig as structural Verilog
module comp_4bit (
  input  B_3,
  input  B_2,
  input  B_1,
  input  B_0,
  input  A_3,
  input  A_2,
  input  A_1,
  input  A_0,
  output OUT
);

  wire and_1_out, and_2_out, xnor_1_out, xnor_2_out, xnor_3_out, xnor_4_out;

  xnor xnor_1 (xnor_1_out, B_3, A_3);
  xnor xnor_2 (xnor_2_out, B_2, A_2);
  xnor xnor_3 (xnor_3_out, B_1, A_1);
  xnor xnor_4 (xnor_4_out, B_0, A_0);
  and and_1 (and_1_out, xnor_1_out, xnor_2_out);
  and and_2 (and_2_out, xnor_3_out, xnor_4_out);
  and and_3 (OUT, and_1_out, and_2_out);
endmodule
