// Digital circuit comp_6bit.dig as structural Verilog
module comp_6bit (
  input  B_3,
  input  B_2,
  input  B_1,
  input  B_0,
  input  A_3,
  input  A_2,
  input  A_1,
  input  A_0,
  input  A_4,
  input  A_5,
  input  B_4,
  input  B_5,
  output OUT
);

  wire and_1_out, and_2_out, and_3_out, and_4_out, xnor_1_out, xnor_2_out, xnor_3_out, xnor_4_out,
       xnor_5_out, xnor_6_out;

  xnor xnor_1 (xnor_1_out, B_5, A_5);
  xnor xnor_2 (xnor_2_out, B_4, A_4);
  xnor xnor_3 (xnor_3_out, B_3, A_3);
  xnor xnor_4 (xnor_4_out, B_2, A_2);
  xnor xnor_5 (xnor_5_out, B_1, A_1);
  xnor xnor_6 (xnor_6_out, B_0, A_0);
  and and_1 (and_1_out, xnor_1_out, xnor_2_out);
  and and_2 (and_2_out, xnor_3_out, xnor_4_out);
  and and_3 (and_3_out, xnor_5_out, xnor_6_out);
  and and_4 (and_4_out, and_2_out, and_3_out);
  and and_5 (OUT, and_1_out, and_4_out);
endmodule
