// Digital circuit hold_signal.dig as structural Verilog
module hold_signal (
  input  CLK,
  input  In,
  input  [3:0] Wait,
  output Out
);

  wire comparator_1_eq, or_1_out;
  wire [3:0] add_1_s, multiplexer_1_out, register_2_q;

  or or_1 (or_1_out, In, comparator_1_eq);
  Register register_1 (.D(In), .C(CLK), .en(or_1_out), .Q(Out));
  Multiplexer #(.Bits(4)) multiplexer_1 (
    .sel(comparator_1_eq), .in_0(add_1_s), .in_1(4'b0000), .out(multiplexer_1_out));
  Register #(.Bits(4)) register_2 (.D(multiplexer_1_out), .C(CLK), .en(Out), .Q(register_2_q));
  Add #(.Bits(4)) add_1 (.a(register_2_q), .b(4'b0000), .c_i(1'b1), .s(add_1_s));  // open: c_o
  Comparator #(.Bits(4)) comparator_1 (.a(add_1_s), .b(Wait), .eq(comparator_1_eq));  // open: gt, lt
endmodule
