// Digital circuit incr_6bit.dig as structural Verilog
module incr_6bit (
  input  IN_5,
  input  IN_4,
  input  IN_3,
  input  IN_2,
  input  IN_1,
  input  IN_0,
  input  EN,
  output OUT_5,
  output OUT_4,
  output OUT_3,
  output OUT_2,
  output OUT_1,
  output OUT_0
);

  wire halfadder_2_c, halfadder_3_c, halfadder_4_c, halfadder_5_c, halfadder_6_c;

  halfAdder halfadder_1 (.A(IN_5), .B(halfadder_2_c), .S(OUT_5));  // open: C
  halfAdder halfadder_2 (.A(IN_4), .B(halfadder_3_c), .S(OUT_4), .C(halfadder_2_c));
  halfAdder halfadder_3 (.A(IN_3), .B(halfadder_4_c), .S(OUT_3), .C(halfadder_3_c));
  halfAdder halfadder_4 (.A(IN_2), .B(halfadder_5_c), .S(OUT_2), .C(halfadder_4_c));
  halfAdder halfadder_5 (.A(IN_1), .B(halfadder_6_c), .S(OUT_1), .C(halfadder_5_c));
  halfAdder halfadder_6 (.A(IN_0), .B(EN), .S(OUT_0), .C(halfadder_6_c));
endmodule
