// Digital circuit scuffed_delay.dig as structural Verilog
module scuffed_delay (
  input  IN,
  output OUT
);

  wire not_1_out, not_2_out, not_3_out, not_4_out, not_5_out;

  not not_1 (not_1_out, IN);
  not not_2 (not_2_out, not_1_out);
  not not_3 (not_3_out, not_2_out);
  not not_4 (not_4_out, not_3_out);
  not not_5 (not_5_out, not_4_out);
  not not_6 (OUT, not_5_out);
endmodule
