// Digital circuit seven_seg_cmpl.dig as structural Verilog
module seven_seg_cmpl (
  input  [3:0] SEG_3,
  input  [3:0] SEG_2,
  input  [3:0] SEG_1,
  input  [3:0] SEG_0,
  input  CLK,
  output a,
  output b,
  output c,
  output d,
  output e,
  output f,
  output g,
  output AN_3,
  output AN_2,
  output AN_1,
  output AN_0
);

  wire [3:0] sw_an_select_1_out;

  an_crtl an_crtl_1 (.CLK(CLK), .AN_3(AN_3), .AN_2(AN_2), .AN_1(AN_1), .AN_0(AN_0));
  sw_an_select sw_an_select_1 (
    .DATA_3(SEG_3), .DATA_2(SEG_2), .DATA_1(SEG_1), .DATA_0(SEG_0), .AN_3(AN_3), .AN_2(AN_2), .AN_1(AN_1),
    .AN_0(AN_0), .OUT(sw_an_select_1_out));
  // sw_2_7seg sw_2_7seg_1: pin names not known; wires that end beside it: sw_an_select_1_out[0], sw_an_select_1_out[1], sw_an_select_1_out[2], sw_an_select_1_out[3], a, b, c, d, e, f, g
endmodule
