// Digital circuit sw_an_select.dig as structural Verilog
module sw_an_select (
  input  [3:0] DATA_3,
  input  [3:0] DATA_2,
  input  [3:0] DATA_1,
  input  [3:0] DATA_0,
  input  AN_3,
  input  AN_2,
  input  AN_1,
  input  AN_0,
  output [3:0] OUT
);

  wire [3:0] and_1_out, and_2_out, and_3_out, and_4_out;

  assign and_1_out = DATA_3 & {4{AN_3}};  // And and_1, 4 bits wide
  assign and_2_out = DATA_2 & {4{AN_2}};  // And and_2, 4 bits wide
  assign and_3_out = DATA_1 & {4{AN_1}};  // And and_3, 4 bits wide
  assign and_4_out = DATA_0 & {4{AN_0}};  // And and_4, 4 bits wide
  assign OUT = and_1_out | and_2_out | and_3_out | and_4_out;  // Or or_1, 4 bits wide
endmodule
