// Digital circuit sw_reg_7seg.dig as structural Verilog
module sw_reg_7seg (
  input  clk
);

  wire an_crtl_1_an_0, an_crtl_1_an_1, an_crtl_1_an_2, an_crtl_1_an_3, button_1_out, sw_2_7seg_1_p5,
       sw_2_7seg_1_p6, sw_2_7seg_1_p7, sw_2_7seg_1_p8, sw_2_7seg_1_p9, sw_2_7seg_1_p10, sw_2_7seg_1_p11;
  wire [3:0] dipswitch_1_out, dipswitch_5_out, dipswitch_9_out, dipswitch_13_out, register_1_q, register_2_q,
       register_3_q, register_4_q, sw_an_select_1_out;

  DipSwitch dipswitch_1 (.out(dipswitch_1_out[0]));
  DipSwitch dipswitch_2 (.out(dipswitch_1_out[1]));
  DipSwitch dipswitch_3 (.out(dipswitch_1_out[2]));
  DipSwitch dipswitch_4 (.out(dipswitch_1_out[3]));
  DipSwitch dipswitch_5 (.out(dipswitch_5_out[0]));
  DipSwitch dipswitch_6 (.out(dipswitch_5_out[1]));
  DipSwitch dipswitch_7 (.out(dipswitch_5_out[2]));
  DipSwitch dipswitch_8 (.out(dipswitch_5_out[3]));
  DipSwitch dipswitch_9 (.out(dipswitch_9_out[0]));
  DipSwitch dipswitch_10 (.out(dipswitch_9_out[1]));
  DipSwitch dipswitch_11 (.out(dipswitch_9_out[2]));
  DipSwitch dipswitch_12 (.out(dipswitch_9_out[3]));
  DipSwitch dipswitch_13 (.out(dipswitch_13_out[0]));
  DipSwitch dipswitch_14 (.out(dipswitch_13_out[1]));
  DipSwitch dipswitch_15 (.out(dipswitch_13_out[2]));
  DipSwitch dipswitch_16 (.out(dipswitch_13_out[3]));
  Button button_1 (.out(button_1_out));
  Register #(.Bits(4)) register_1 (.D(dipswitch_1_out), .C(button_1_out), .en(button_1_out), .Q(register_1_q));
  Register #(.Bits(4)) register_2 (.D(dipswitch_5_out), .C(button_1_out), .en(button_1_out), .Q(register_2_q));
  Register #(.Bits(4)) register_3 (.D(dipswitch_9_out), .C(button_1_out), .en(button_1_out), .Q(register_3_q));
  Register #(.Bits(4)) register_4 (.D(dipswitch_13_out), .C(button_1_out), .en(button_1_out), .Q(register_4_q));
  an_crtl an_crtl_1 (
    .CLK(clk), .AN_3(an_crtl_1_an_3), .AN_2(an_crtl_1_an_2), .AN_1(an_crtl_1_an_1), .AN_0(an_crtl_1_an_0));
  sw_an_select sw_an_select_1 (
    .DATA_3(register_1_q), .DATA_2(register_2_q), .DATA_1(register_3_q), .DATA_0(register_4_q),
    .AN_3(an_crtl_1_an_3), .AN_2(an_crtl_1_an_2), .AN_1(an_crtl_1_an_1), .AN_0(an_crtl_1_an_0),
    .OUT(sw_an_select_1_out));
  // sw_2_7seg sw_2_7seg_1: pin names not known; wires that end beside it: sw_an_select_1_out[0], sw_an_select_1_out[1], sw_an_select_1_out[2], sw_an_select_1_out[3], sw_2_7seg_1_p5, sw_2_7seg_1_p6, sw_2_7seg_1_p7, sw_2_7seg_1_p8, sw_2_7seg_1_p9, sw_2_7seg_1_p10, sw_2_7seg_1_p11
  Seven_Seg #(.commonCathode("true"), .commonConnectionType("anode")) seven_seg_1 (
    .a(sw_2_7seg_1_p5), .b(sw_2_7seg_1_p6), .c(sw_2_7seg_1_p7), .d(sw_2_7seg_1_p8), .e(sw_2_7seg_1_p9),
    .f(sw_2_7seg_1_p10), .g(sw_2_7seg_1_p11), .dp(1'b0), .common(an_crtl_1_an_3));
  Seven_Seg #(.commonCathode("true"), .commonConnectionType("anode")) seven_seg_2 (
    .a(sw_2_7seg_1_p5), .b(sw_2_7seg_1_p6), .c(sw_2_7seg_1_p7), .d(sw_2_7seg_1_p8), .e(sw_2_7seg_1_p9),
    .f(sw_2_7seg_1_p10), .g(sw_2_7seg_1_p11), .dp(1'b0), .common(an_crtl_1_an_2));
  Seven_Seg #(.commonCathode("true"), .commonConnectionType("anode")) seven_seg_3 (
    .a(sw_2_7seg_1_p5), .b(sw_2_7seg_1_p6), .c(sw_2_7seg_1_p7), .d(sw_2_7seg_1_p8), .e(sw_2_7seg_1_p9),
    .f(sw_2_7seg_1_p10), .g(sw_2_7seg_1_p11), .dp(1'b0), .common(an_crtl_1_an_1));
  Seven_Seg #(.commonCathode("true"), .commonConnectionType("anode")) seven_seg_4 (
    .a(sw_2_7seg_1_p5), .b(sw_2_7seg_1_p6), .c(sw_2_7seg_1_p7), .d(sw_2_7seg_1_p8), .e(sw_2_7seg_1_p9),
    .f(sw_2_7seg_1_p10), .g(sw_2_7seg_1_p11), .dp(1'b0), .common(an_crtl_1_an_0));

  // Notes on the sheet:
  //   clk: Hz: 24
endmodule
