// Digital circuit async_4bit_counter.dig as structural Verilog
module async_4bit_counter (
  input  IN,
  output S0,
  output S1,
  output S2,
  output S3
);

  wire d_ff_1_nq, d_ff_2_nq, d_ff_3_nq, d_ff_4_nq;

  D_FF d_ff_1 (.D(d_ff_1_nq), .C(IN), .Q(S0), .nQ(d_ff_1_nq));
  D_FF d_ff_2 (.D(d_ff_2_nq), .C(d_ff_1_nq), .Q(S1), .nQ(d_ff_2_nq));
  D_FF d_ff_3 (.D(d_ff_3_nq), .C(d_ff_2_nq), .Q(S2), .nQ(d_ff_3_nq));
  D_FF d_ff_4 (.D(d_ff_4_nq), .C(d_ff_3_nq), .Q(S3), .nQ(d_ff_4_nq));
endmodule
