// Digital circuit rcAdder_8bit.dig as structural Verilog
module rcAdder_8bit (
  input  B0,
  input  A0,
  input  Ci,
  input  B1,
  input  A1,
  input  B2,
  input  A2,
  input  B3,
  input  A3,
  input  B4,
  input  A4,
  input  B5,
  input  A5,
  input  B6,
  input  A6,
  input  B7,
  input  A7,
  output Co,
  output S3,
  output S2,
  output S1,
  output S0,
  output S7,
  output S6,
  output S5,
  output S4
);

  wire fulladder_2_co, fulladder_3_co, fulladder_4_co, fulladder_5_co, fulladder_6_co, fulladder_7_co,
       fulladder_8_co;

  fullAdder fulladder_1 (.A(A7), .B(B7), .Ci(fulladder_2_co), .Co(Co), .S(S7));
  fullAdder fulladder_2 (.A(A6), .B(B6), .Ci(fulladder_3_co), .Co(fulladder_2_co), .S(S6));
  fullAdder fulladder_3 (.A(A5), .B(B5), .Ci(fulladder_4_co), .Co(fulladder_3_co), .S(S5));
  fullAdder fulladder_4 (.A(A4), .B(B4), .Ci(fulladder_5_co), .Co(fulladder_4_co), .S(S4));
  fullAdder fulladder_5 (.A(A3), .B(B3), .Ci(fulladder_6_co), .Co(fulladder_5_co), .S(S3));
  fullAdder fulladder_6 (.A(A2), .B(B2), .Ci(fulladder_7_co), .Co(fulladder_6_co), .S(S2));
  fullAdder fulladder_7 (.A(A1), .B(B1), .Ci(fulladder_8_co), .Co(fulladder_7_co), .S(S1));
  fullAdder fulladder_8 (.A(A0), .B(B0), .Ci(Ci), .Co(fulladder_8_co), .S(S0));
endmodule

/* Test case:
	Ci A7 A6 A5 A4 A3 A2 A1 A0 B7 B6 B5 B4 B3 B2 B1 B0 Co S7 S6 S5 S4 S3 S2 S1 S0

loop(A, 64)
    loop(B, 64)
        0 bits(8, A)   bits(8, B)  bits(9, A+B)
        1 bits(8, A)   bits(8, B)  bits(9, A+B+1)
    end loop
end loop
*/
