// Digital circuit async_4bit_counter.dig as structural Verilog
module async_4bit_counter (
  input  IN,
  output S0,
  output S1,
  output S2,
  output S3
);

  wire jk_ff_as_1_q, jk_ff_as_2_q, jk_ff_as_3_q, not_1_out;

  not not_1 (not_1_out, 1'b1);
  JK_FF_AS jk_ff_as_1 (.Set(not_1_out), .J(1'b1), .C(IN), .K(1'b1), .Clr(not_1_out), .Q(jk_ff_as_1_q), .nQ(S0));
  JK_FF_AS jk_ff_as_2 (
    .Set(not_1_out), .J(1'b1), .C(jk_ff_as_1_q), .K(1'b1), .Clr(not_1_out), .Q(jk_ff_as_2_q), .nQ(S1));
  JK_FF_AS jk_ff_as_3 (
    .Set(not_1_out), .J(1'b1), .C(jk_ff_as_2_q), .K(1'b1), .Clr(not_1_out), .Q(jk_ff_as_3_q), .nQ(S2));
  JK_FF_AS jk_ff_as_4 (.Set(not_1_out), .J(1'b1), .C(jk_ff_as_3_q), .K(1'b1), .Clr(not_1_out), .nQ(S3));  // open: Q
endmodule
