// Digital circuit fullAdder.dig as structural Verilog
module fullAdder (
  input  A,
  input  B,
  input  Ci,
  output Co,
  output S
);

  wire halfadder_1_c, halfadder_2_c, halfadder_2_s;

  halfAdder halfadder_1 (.A(Ci), .B(halfadder_2_s), .S(S), .C(halfadder_1_c));
  halfAdder halfadder_2 (.A(A), .B(B), .S(halfadder_2_s), .C(halfadder_2_c));
  or or_1 (Co, halfadder_1_c, halfadder_2_c);
endmodule

/* Test case:
A B Ci  Co S
0 0 0   0  0
0 0 1   0  1
0 1 0   0  1
0 1 1   1  0
1 0 0   0  1
1 0 1   1  0
1 1 0   1  0
1 1 1   1  1
*/
