// Digital circuit rcAdder.dig as structural Verilog
module rcAdder (
  input  B0,
  input  A0,
  input  Ci,
  input  B1,
  input  A1,
  input  B2,
  input  A2,
  input  B3,
  input  A3,
  output Co,
  output S3,
  output S2,
  output S1,
  output S0
);

  wire fulladder_2_co, fulladder_3_co, fulladder_4_co;

  fullAdder fulladder_1 (.A(A3), .B(B3), .Ci(fulladder_2_co), .Co(Co), .S(S3));
  fullAdder fulladder_2 (.A(A2), .B(B2), .Ci(fulladder_3_co), .Co(fulladder_2_co), .S(S2));
  fullAdder fulladder_3 (.A(A1), .B(B1), .Ci(fulladder_4_co), .Co(fulladder_3_co), .S(S1));
  fullAdder fulladder_4 (.A(A0), .B(B0), .Ci(Ci), .Co(fulladder_4_co), .S(S0));
endmodule

/* Test case:
	Ci A3 A2 A1 A0 B3 B2 B1 B0 Co S3 S2 S1 S0

loop(A, 16)
    loop(B, 16)
        0 bits(4, A)   bits(4, B)  bits(5, A+B)
        1 bits(4, A)   bits(4, B)  bits(5, A+B+1)
    end loop
end loop
*/
