// Digital circuit sync_4bit_counter.dig as structural Verilog
module sync_4bit_counter (
  input  IN,
  output S3,
  output S2,
  output S1,
  output S0
);

  wire and_1_out, and_2_out;

  JK_FF jk_ff_1 (.J(1'b1), .C(IN), .K(1'b1), .Q(S0));  // open: nQ
  JK_FF jk_ff_2 (.J(S0), .C(IN), .K(S0), .Q(S1));  // open: nQ
  and and_1 (and_1_out, S1, S0);
  JK_FF jk_ff_3 (.J(and_1_out), .C(IN), .K(and_1_out), .Q(S2));  // open: nQ
  and and_2 (and_2_out, S2, and_1_out);
  JK_FF jk_ff_4 (.J(and_2_out), .C(IN), .K(and_2_out), .Q(S3));  // open: nQ
endmodule
